# Fritzing sketch Green House (saved by Fritzing 0.9.6b)
breadboards: 1

parts:
  Arduino_UNO = Arduino Uno (Rev3)
  DHT11 = DHT11 Humitidy and Temperature Sensor
  RGB_LED = RGB LED - (4 legs) [package="5 mm [THT]"]
  LED = smd LED [color="White (4500K)" package="1206 [SMD]"]
  Buzzer = Passive Buzzer
  Soil_Sensor = Soil Moisture Sensor
  LDR_Sensor = Photocell (LDR) [package=THT]
  NodeMCU = NodeMCU V1.0
  FAN = Fan - Ventilador [package=THT]
  Water_Level_Sensor = Water Level Sensor
  Relay = Keyes Relay [package=THT]
  Relay_2 = Keyes Relay [package=THT]
  WATER_PUMP = water pump/motor  # not connected

nets:
  N1: Arduino_UNO.A0, LDR_Sensor.pin_1
  N2: Arduino_UNO.A1, Soil_Sensor.SIG
  N3: Arduino_UNO.A2, Water_Level_Sensor.SIG
  N4: Arduino_UNO.D8, RGB_LED.red_cathode
  N5: Arduino_UNO.D9_PWM, Relay_2.signal
  VCC: Arduino_UNO.D10_PWM/SS, Arduino_UNO.5V, DHT11.VDD, DHT11.DATA, Buzzer.NC, Soil_Sensor.VCC, LDR_Sensor.pin_0, NodeMCU.Vin, Water_Level_Sensor.VCC, Relay.power, Relay.NO, Relay_2.power
  N6: Arduino_UNO.D11_PWM/MOSI, Buzzer.S
  N7: Arduino_UNO.D12/MISO, Relay.signal
  N8: Arduino_UNO.D13/SCK, LED.anode
  N9: Arduino_UNO.D0/RX, NodeMCU.D2
  N10: Arduino_UNO.D1/TX, NodeMCU.D1
  N11: Arduino_UNO.D2, NodeMCU.TX
  N12: Arduino_UNO.D3_PWM, NodeMCU.RX
  N13: Arduino_UNO.D5_PWM, RGB_LED.green_cathode
  N14: Arduino_UNO.D6_PWM, RGB_LED.blue_cathode
  GND: Arduino_UNO.GND, DHT11.GND, RGB_LED.common_anode, LED.cathode, Buzzer.-, Soil_Sensor.GND, NodeMCU.GND, FAN.GND, Water_Level_Sensor.GND, Relay.ground, Relay_2.ground
  N15: FAN.5V, Relay.C

custom parts:
  DHT11 Humitidy and Temperature Sensor: DHT11 Humidity and Temperature Sensor
  NodeMCU V1.0: ESP8266 based NodeMCU
  Fan - Ventilador: Ventilador de 2 pines, se encuentra comunmente en computadoras de escritorio
  Water Level Sensor: A water level sensor. This sensor operates at 3V to 5V. The Sig (signal) pin outputs an analogue signal that is in proportion to the amount of water in contact with the sensor.
  Keyes Relay: The Keyes 5V relay module is suitable for SCM development, home appliance control. It uses a 5V~12V TIL control signal which can control DC / AC signal.
  water pump/motor: WATER PUMP BY ARDUBLOCKTR
